// Logisim project TheLife.circ as structural Verilog: 10 circuits, main circuit main
module main (
);

  wire button_2_out, button_3_out, button_4_out, button_5_out, button_6_out, button_7_out, button_8_out,
       button_9_out, button_out, OK_out;
  wire [8:0] buttons_1_out_27;
  wire [15:0] buttons_1_out_11, buttons_1_out_12, buttons_1_out_13, buttons_1_out_14, buttons_1_out_15,
       buttons_1_out_16, buttons_1_out_17, buttons_1_out_18, buttons_1_out_19, buttons_1_out_20,
       buttons_1_out_21, buttons_1_out_22, buttons_1_out_23, buttons_1_out_24, buttons_1_out_25,
       buttons_1_out_26;

  DotMatrix #(.matrixcols(16), .matrixrows(16)) dotmatrix_1 (
    .col0(buttons_1_out_11), .col1(buttons_1_out_19), .col2(buttons_1_out_12), .col3(buttons_1_out_20),
    .col4(buttons_1_out_13), .col5(buttons_1_out_21), .col6(buttons_1_out_14), .col7(buttons_1_out_22),
    .col8(buttons_1_out_15), .col9(buttons_1_out_23), .col10(buttons_1_out_16), .col11(buttons_1_out_24),
    .col12(buttons_1_out_17), .col13(buttons_1_out_25), .col14(buttons_1_out_18), .col15(buttons_1_out_26));
  BUTTONS buttons_1 (
    .u(button_out), .ok(OK_out), .l(button_3_out), .r(button_2_out), .d(button_4_out), .start(button_6_out),
    .reset(button_7_out), .glider(button_5_out), .pause(button_8_out), .out_11(buttons_1_out_11),
    .out_19(buttons_1_out_19), .out_12(buttons_1_out_12), .out_20(buttons_1_out_20),
    .out_13(buttons_1_out_13), .out_21(buttons_1_out_21), .out_14(buttons_1_out_14),
    .out_22(buttons_1_out_22), .out_27(buttons_1_out_27), .out_15(buttons_1_out_15),
    .out_23(buttons_1_out_23), .out_16(buttons_1_out_16), .out_24(buttons_1_out_24),
    .out_17(buttons_1_out_17), .out_25(buttons_1_out_25), .out_18(buttons_1_out_18),
    .out_26(buttons_1_out_26), .pause_2(button_9_out));
  Button button (.out(button_out));
  Button OK (.out(OK_out));
  Button button_2 (.out(button_2_out));
  Button button_3 (.out(button_3_out));
  Button button_4 (.out(button_4_out));
  Button button_5 (.out(button_5_out));
  Button button_6 (.out(button_6_out));
  Button button_7 (.out(button_7_out));
  // Probe on buttons_1_out_27
  Button button_8 (.out(button_8_out));
  Button button_9 (.out(button_9_out));

  // Notes on the sheet:
  //   Use buttons to move the cursor.
  //   Cell in the center is already set to be alive. Cursor is at the center too.
  //   If you reset the game, cursor will return to the center
  //   If you press GLIDER, glider will appear at the center.
  //   Cursor will return to the center like in the beginning.
  //   You can pause the game but to edit the cells you need to reset the game.
  //   RESET
  //   GLIDER
  //   START
  //   Cells alive
  //   PAUSE
  //   EXPLOSION
endmodule

module Cell (
  input  can_play,
  input  upper_center,
  input  upper_left,
  input  upper_right,
  input  left,
  input  right,
  input  bottom_left,
  input  bottom_right,
  input  bottom_center,
  input  pressed,
  input  tick,
  output State
);

  State_manager state_manager_1 (
    .can_play(can_play), .nb1(upper_center), .nb2(upper_left), .nb3(upper_right), .nb4(left), .nb5(right),
    .nb6(bottom_left), .nb7(bottom_right), .nb8(bottom_center), .user_s_hand(pressed), .tick(tick),
    .State(State));

  // Notes on the sheet:
  //   We collect all conditions of our neighbours, user's commands, ticks and flag to play the game
endmodule

module State_manager (
  input  can_play,
  input  nb1,
  input  nb2,
  input  nb3,
  input  nb4,
  input  nb5,
  input  nb6,
  input  nb7,
  input  nb8,
  input  user_s_hand,
  input  tick,
  output State
);

  wire and_1_out, and_2_out, and_3_out, and_4_out, and_5_out, and_6_out, and_7_out, not_1_out, not_2_out,
       not_3_out, not_4_out, not_6_out, not_7_out, or_1_out, or_2_out, register_1_q;
  wire [1:0] adder_1_out, adder_2_out, adder_3_out, adder_4_out, adder_5_out, adder_6_out;
  wire [2:0] adder_7_out;
  wire [2:2] adder_5_cout, adder_6_cout;

  Adder #(.width(1)) adder_1 (.a(nb1), .b(nb2), .out(adder_1_out[0]), .cout(adder_1_out[1]));  // open: cin
  Adder #(.width(1)) adder_2 (.a(nb3), .b(nb4), .out(adder_2_out[0]), .cout(adder_2_out[1]));  // open: cin
  Adder #(.width(1)) adder_3 (.a(nb5), .b(nb6), .out(adder_3_out[0]), .cout(adder_3_out[1]));  // open: cin
  Adder #(.width(1)) adder_4 (.a(nb7), .b(nb8), .out(adder_4_out[0]), .cout(adder_4_out[1]));  // open: cin
  Adder #(.width(2)) adder_5 (
    .a(adder_1_out), .b(adder_2_out), .out(adder_5_out), .cout(adder_5_cout[2]));  // open: cin
  Adder #(.width(2)) adder_6 (
    .a(adder_3_out), .b(adder_4_out), .out(adder_6_out), .cout(adder_6_cout[2]));  // open: cin
  Adder #(.width(3)) adder_7 (
    .a({adder_5_cout[2], adder_5_out}), .b({adder_6_cout[2], adder_6_out}), .out(adder_7_out));  // open: cin, cout
  not not_1 (not_1_out, adder_7_out[2]);
  not not_2 (not_2_out, adder_7_out[0]);
  and and_1 (and_1_out, adder_7_out[0], adder_7_out[1], not_1_out);
  and and_2 (and_2_out, not_1_out, adder_7_out[1], not_2_out);
  and and_3 (and_3_out, user_s_hand, tick);
  or or_1 (or_1_out, and_1_out, and_2_out);
  not not_3 (not_3_out, register_1_q);
  and and_4 (and_4_out, can_play, and_5_out);
  and and_5 (and_5_out, and_1_out, not_3_out);
  and and_6 (and_6_out, can_play, and_7_out);
  and and_7 (and_7_out, register_1_q, or_1_out);
  or or_2 (or_2_out, and_4_out, and_6_out, and_3_out);
  Register #(.width(1), .trigger("falling")) register_1 (.D(or_2_out), .Q(register_1_q), .clk(tick));  // open: en, clr
  not not_4 (not_4_out, register_1_q);
  not not_5 (State, not_7_out);
  not not_6 (not_6_out, not_4_out);
  not not_7 (not_7_out, not_6_out);

  // Notes on the sheet:
  //   Соседи
  //   3 alive
  //   2 alive
  //   User's command
  //   Not to switch statement
  //   Continue existing
  //   Becoming alive + no commands from user
endmodule

module Row_of_cells (
  input  [15:0] Top,
  input  can_play,
  input  tick,
  input  [15:0] Down,
  input  [15:0] Pressed,
  output [15:0] Alive_counter,
  output [15:0] Display
);

  Cell cell_1 (
    .upper_center(Top[0]), .upper_left(Top[15]), .upper_right(Top[1]), .left(Alive_counter[15]),
    .right(Alive_counter[1]), .bottom_left(Down[15]), .bottom_right(Down[1]), .bottom_center(Down[0]),
    .pressed(Pressed[0]), .tick(tick), .State(Alive_counter[0]), .can_play(can_play));
  Cell cell_2 (
    .upper_center(Top[1]), .upper_left(Top[0]), .upper_right(Top[2]), .left(Alive_counter[0]),
    .right(Alive_counter[2]), .bottom_left(Down[0]), .bottom_right(Down[2]), .bottom_center(Down[1]),
    .pressed(Pressed[1]), .tick(tick), .State(Alive_counter[1]), .can_play(can_play));
  Cell cell_3 (
    .upper_center(Top[2]), .upper_left(Top[1]), .upper_right(Top[3]), .left(Alive_counter[1]),
    .right(Alive_counter[3]), .bottom_left(Down[1]), .bottom_right(Down[3]), .bottom_center(Down[2]),
    .pressed(Pressed[2]), .tick(tick), .State(Alive_counter[2]), .can_play(can_play));
  Cell cell_4 (
    .upper_center(Top[3]), .upper_left(Top[2]), .upper_right(Top[4]), .left(Alive_counter[2]),
    .right(Alive_counter[4]), .bottom_left(Down[2]), .bottom_right(Down[4]), .bottom_center(Down[3]),
    .pressed(Pressed[3]), .tick(tick), .State(Alive_counter[3]), .can_play(can_play));
  Cell cell_5 (
    .upper_center(Top[4]), .upper_left(Top[3]), .upper_right(Top[5]), .left(Alive_counter[3]),
    .right(Alive_counter[5]), .bottom_left(Down[3]), .bottom_right(Down[5]), .bottom_center(Down[4]),
    .pressed(Pressed[4]), .tick(tick), .State(Alive_counter[4]), .can_play(can_play));
  Cell cell_6 (
    .upper_center(Top[5]), .upper_left(Top[4]), .upper_right(Top[6]), .left(Alive_counter[4]),
    .right(Alive_counter[6]), .bottom_left(Down[4]), .bottom_right(Down[6]), .bottom_center(Down[5]),
    .pressed(Pressed[5]), .tick(tick), .State(Alive_counter[5]), .can_play(can_play));
  Cell cell_7 (
    .upper_center(Top[6]), .upper_left(Top[5]), .upper_right(Top[7]), .left(Alive_counter[5]),
    .right(Alive_counter[7]), .bottom_left(Down[5]), .bottom_right(Down[7]), .bottom_center(Down[6]),
    .pressed(Pressed[6]), .tick(tick), .State(Alive_counter[6]), .can_play(can_play));
  Cell cell_8 (
    .upper_center(Top[7]), .upper_left(Top[6]), .upper_right(Top[8]), .left(Alive_counter[6]),
    .right(Alive_counter[8]), .bottom_left(Down[6]), .bottom_right(Down[8]), .bottom_center(Down[7]),
    .pressed(Pressed[7]), .tick(tick), .State(Alive_counter[7]), .can_play(can_play));
  Cell cell_9 (
    .upper_center(Top[8]), .upper_left(Top[7]), .upper_right(Top[9]), .left(Alive_counter[7]),
    .right(Alive_counter[9]), .bottom_left(Down[7]), .bottom_right(Down[9]), .bottom_center(Down[8]),
    .pressed(Pressed[8]), .tick(tick), .State(Alive_counter[8]), .can_play(can_play));
  Cell cell_10 (
    .upper_center(Top[9]), .upper_left(Top[8]), .upper_right(Top[10]), .left(Alive_counter[8]),
    .right(Alive_counter[10]), .bottom_left(Down[8]), .bottom_right(Down[10]), .bottom_center(Down[9]),
    .pressed(Pressed[9]), .tick(tick), .State(Alive_counter[9]), .can_play(can_play));
  Cell cell_11 (
    .upper_center(Top[10]), .upper_left(Top[9]), .upper_right(Top[11]), .left(Alive_counter[9]),
    .right(Alive_counter[11]), .bottom_left(Down[9]), .bottom_right(Down[11]), .bottom_center(Down[10]),
    .pressed(Pressed[10]), .tick(tick), .State(Alive_counter[10]), .can_play(can_play));
  Cell cell_12 (
    .upper_center(Top[11]), .upper_left(Top[10]), .upper_right(Top[12]), .left(Alive_counter[10]),
    .right(Alive_counter[12]), .bottom_left(Down[10]), .bottom_right(Down[12]), .bottom_center(Down[11]),
    .pressed(Pressed[11]), .tick(tick), .State(Alive_counter[11]), .can_play(can_play));
  Cell cell_13 (
    .upper_center(Top[12]), .upper_left(Top[11]), .upper_right(Top[13]), .left(Alive_counter[11]),
    .right(Alive_counter[13]), .bottom_left(Down[11]), .bottom_right(Down[13]), .bottom_center(Down[12]),
    .pressed(Pressed[12]), .tick(tick), .State(Alive_counter[12]), .can_play(can_play));
  Cell cell_14 (
    .upper_center(Top[13]), .upper_left(Top[12]), .upper_right(Top[14]), .left(Alive_counter[12]),
    .right(Alive_counter[14]), .bottom_left(Down[12]), .bottom_right(Down[14]), .bottom_center(Down[13]),
    .pressed(Pressed[13]), .tick(tick), .State(Alive_counter[13]), .can_play(can_play));
  Cell cell_15 (
    .upper_center(Top[14]), .upper_left(Top[13]), .upper_right(Top[15]), .left(Alive_counter[13]),
    .right(Alive_counter[15]), .bottom_left(Down[13]), .bottom_right(Down[15]), .bottom_center(Down[14]),
    .pressed(Pressed[14]), .tick(tick), .State(Alive_counter[14]), .can_play(can_play));
  Cell cell_16 (
    .upper_center(Top[15]), .upper_left(Top[14]), .upper_right(Top[0]), .left(Alive_counter[14]),
    .right(Alive_counter[0]), .bottom_left(Down[14]), .bottom_right(Down[0]), .bottom_center(Down[15]),
    .pressed(Pressed[15]), .tick(tick), .State(Alive_counter[15]), .can_play(can_play));

  assign Display = Alive_counter;

  // Notes on the sheet:
  //   Top row of neighbors ->
  //   Bottom row of neighbors
  //   User's impact
  //   tick
  //   can play
  //   can play
  //   tick
  //   can play
  //   tick
  //   can play
  //   tick
  //   can play
  //   tick
  //   can play
  //   tick
  //   can play
  //   tick
  //   can play
  //   tick
  //   Output all cell's states
endmodule

module Rows_plate (
  input  tick,
  input  [15:0] Pressed_1,
  input  [15:0] Pressed_2,
  input  [15:0] Pressed_3,
  input  [15:0] Pressed_4,
  input  [15:0] Pressed_5,
  input  [15:0] Pressed_6,
  input  [15:0] Pressed_7,
  input  [15:0] Pressed_8,
  input  [15:0] Pressed_9,
  input  [15:0] Pressed_10,
  input  [15:0] Pressed_11,
  input  [15:0] Pressed_12,
  input  [15:0] Pressed_13,
  input  [15:0] Pressed_14,
  input  [15:0] Pressed_15,
  input  [15:0] Pressed_16,
  output [15:0] out_1,
  output [15:0] out_2,
  output [15:0] out_3,
  output [15:0] out_4,
  output [15:0] out_5,
  output [15:0] out_6,
  output [15:0] out_7,
  output [15:0] out_8,
  output [15:0] out_9,
  output [15:0] out_10,
  output [15:0] out_11,
  output [15:0] out_12,
  output [15:0] out_13,
  output [15:0] out_14,
  output [15:0] out_15,
  output [15:0] out_16,
  output [8:0] alive
);

  wire and_1_out;
  wire [8:0] pressedcounter_1_ouot;
  wire [15:0] row_of_cells_1_alive_counter, row_of_cells_2_alive_counter, row_of_cells_3_alive_counter,
       row_of_cells_4_alive_counter, row_of_cells_5_alive_counter, row_of_cells_6_alive_counter,
       row_of_cells_7_alive_counter, row_of_cells_8_alive_counter, row_of_cells_9_alive_counter,
       row_of_cells_10_alive_counter, row_of_cells_11_alive_counter, row_of_cells_12_alive_counter,
       row_of_cells_13_alive_counter, row_of_cells_14_alive_counter, row_of_cells_15_alive_counter,
       row_of_cells_16_alive_counter;

  Row_of_cells row_of_cells_1 (
    .tick(tick), .Pressed(Pressed_1), .Display(out_1), .Top(out_16), .Down(out_2), .can_play(and_1_out),
    .Alive_counter(row_of_cells_1_alive_counter));
  Row_of_cells row_of_cells_2 (
    .tick(tick), .Pressed(Pressed_2), .Display(out_2), .Top(out_1), .Down(out_3), .can_play(and_1_out),
    .Alive_counter(row_of_cells_2_alive_counter));
  Row_of_cells row_of_cells_3 (
    .tick(tick), .Pressed(Pressed_3), .Display(out_3), .Top(out_2), .Down(out_4), .can_play(and_1_out),
    .Alive_counter(row_of_cells_3_alive_counter));
  Row_of_cells row_of_cells_4 (
    .tick(tick), .Pressed(Pressed_4), .Display(out_4), .Top(out_3), .Down(out_5), .can_play(and_1_out),
    .Alive_counter(row_of_cells_4_alive_counter));
  Row_of_cells row_of_cells_5 (
    .tick(tick), .Pressed(Pressed_5), .Display(out_5), .Top(out_4), .Down(out_6), .can_play(and_1_out),
    .Alive_counter(row_of_cells_5_alive_counter));
  Row_of_cells row_of_cells_6 (
    .tick(tick), .Pressed(Pressed_6), .Display(out_6), .Top(out_5), .Down(out_7), .can_play(and_1_out),
    .Alive_counter(row_of_cells_6_alive_counter));
  Row_of_cells row_of_cells_7 (
    .tick(tick), .Pressed(Pressed_7), .Display(out_7), .Top(out_6), .Down(out_8), .can_play(and_1_out),
    .Alive_counter(row_of_cells_7_alive_counter));
  Row_of_cells row_of_cells_8 (
    .tick(tick), .Pressed(Pressed_8), .Display(out_8), .Top(out_7), .Down(out_9), .can_play(and_1_out),
    .Alive_counter(row_of_cells_8_alive_counter));
  Row_of_cells row_of_cells_9 (
    .tick(tick), .Pressed(Pressed_9), .Display(out_9), .Top(out_8), .Down(out_10), .can_play(and_1_out),
    .Alive_counter(row_of_cells_9_alive_counter));
  Row_of_cells row_of_cells_10 (
    .tick(tick), .Pressed(Pressed_10), .Display(out_10), .Top(out_9), .Down(out_11), .can_play(and_1_out),
    .Alive_counter(row_of_cells_10_alive_counter));
  Row_of_cells row_of_cells_11 (
    .tick(tick), .Pressed(Pressed_11), .Display(out_11), .Top(out_10), .Down(out_12), .can_play(and_1_out),
    .Alive_counter(row_of_cells_11_alive_counter));
  Row_of_cells row_of_cells_12 (
    .tick(tick), .Pressed(Pressed_12), .Display(out_12), .Top(out_11), .Down(out_13), .can_play(and_1_out),
    .Alive_counter(row_of_cells_12_alive_counter));
  Row_of_cells row_of_cells_13 (
    .tick(tick), .Pressed(Pressed_13), .Display(out_13), .Top(out_12), .Down(out_14), .can_play(and_1_out),
    .Alive_counter(row_of_cells_13_alive_counter));
  Row_of_cells row_of_cells_14 (
    .tick(tick), .Pressed(Pressed_14), .Display(out_14), .Top(out_13), .Down(out_15), .can_play(and_1_out),
    .Alive_counter(row_of_cells_14_alive_counter));
  Row_of_cells row_of_cells_15 (
    .tick(tick), .Pressed(Pressed_15), .Display(out_15), .Top(out_14), .Down(out_16), .can_play(and_1_out),
    .Alive_counter(row_of_cells_15_alive_counter));
  Row_of_cells row_of_cells_16 (
    .tick(tick), .Pressed(Pressed_16), .Display(out_16), .Top(out_15), .Down(out_1), .can_play(and_1_out),
    .Alive_counter(row_of_cells_16_alive_counter));
  PressedCounter pressedcounter_1 (
    .Pressed_1(Pressed_1), .Pressed_2(Pressed_2), .Pressed_3(Pressed_3), .Pressed_4(Pressed_4),
    .Pressed_5(Pressed_5), .Pressed_6(Pressed_6), .Pressed_7(Pressed_7), .Pressed_8(Pressed_8),
    .Pressed_9(Pressed_9), .Pressed_10(Pressed_10), .Pressed_11(Pressed_11), .Pressed_12(Pressed_12),
    .Pressed_13(Pressed_13), .Pressed_14(Pressed_14), .Pressed_15(Pressed_15), .Pressed_16(Pressed_16),
    .ouot(pressedcounter_1_ouot));
  and and_1 (and_1_out, ~pressedcounter_1_ouot[8], ~pressedcounter_1_ouot[7], ~pressedcounter_1_ouot[6], ~pressedcounter_1_ouot[5], ~pressedcounter_1_ouot[4], ~pressedcounter_1_ouot[3], ~pressedcounter_1_ouot[2], ~pressedcounter_1_ouot[1], ~pressedcounter_1_ouot[0]);  // AND_Gate
  // Probe on pressedcounter_1_ouot
  PressedCounter pressedcounter_2 (
    .Pressed_1(row_of_cells_1_alive_counter), .Pressed_2(row_of_cells_2_alive_counter),
    .Pressed_3(row_of_cells_3_alive_counter), .Pressed_4(row_of_cells_4_alive_counter),
    .Pressed_5(row_of_cells_5_alive_counter), .Pressed_6(row_of_cells_6_alive_counter),
    .Pressed_7(row_of_cells_7_alive_counter), .Pressed_8(row_of_cells_8_alive_counter),
    .Pressed_9(row_of_cells_9_alive_counter), .Pressed_10(row_of_cells_10_alive_counter),
    .Pressed_11(row_of_cells_11_alive_counter), .Pressed_12(row_of_cells_12_alive_counter),
    .Pressed_13(row_of_cells_13_alive_counter), .Pressed_14(row_of_cells_14_alive_counter),
    .Pressed_15(row_of_cells_15_alive_counter), .Pressed_16(row_of_cells_16_alive_counter), .ouot(alive));
  // Probe on alive

  // Notes on the sheet:
  //   If no commands from user, we can play
endmodule

module Controller (
  input  [7:0] \input ,
  output [15:0] out_1,
  output [15:0] out_2,
  output [15:0] out_3,
  output [15:0] out_4,
  output [15:0] out_5,
  output [15:0] out_6,
  output [15:0] out_7,
  output [15:0] out_8,
  output [15:0] out_9,
  output [15:0] out_10,
  output [15:0] out_11,
  output [15:0] out_12,
  output [15:0] out_13,
  output [15:0] out_14,
  output [15:0] out_15,
  output [15:0] out_16,
  output tick
);

  wire and_1_out, and_2_out, and_3_out, cdm_8_mark5_1_p4, cdm_8_mark5_1_p5, cdm_8_mark5_1_p7,
       cdm_8_mark5_1_p8, cdm_8_mark5_1_p9, cdm_8_mark5_1_p10, cdm_8_mark5_1_p11, cdm_8_mark5_1_p12,
       cdm_8_mark5_1_p13, clk, decoder_1_out0, decoder_1_out1, decoder_2_out0, decoder_2_out1, I_O_0_out,
       IAck, IOsel, IRQ, not_1_out, not_2_out, READwrite;
  wire [2:0] vec;
  wire [4:0] IOaddr;
  wire [6:0] controlled_buffer_4_out;
  wire [7:0] cdm_8_mark5_1_p15_2, cdm_8_mark5_1_p16, cdm_8_mark5_1_p17, IOdat;
  wire [7:5] cdm_8_mark5_1_p15;

  Clock clock_1 (.out(clk));
  and and_1 (and_1_out, ~IOaddr[4], cdm_8_mark5_1_p15[5], cdm_8_mark5_1_p15[6], cdm_8_mark5_1_p15[7], decoder_1_out1);  // AND_Gate
  or or_1 (IOsel, and_1_out, and_2_out);
  // Probe on cdm_8_mark5_1_p8
  // Probe on cdm_8_mark5_1_p7
  // Probe on cdm_8_mark5_1_p5
  // Probe on cdm_8_mark5_1_p4
  // Probe on cdm_8_mark5_1_p9
  and and_2 (and_2_out, ~IOaddr[0], ~IOaddr[1], ~IOaddr[2], ~IOaddr[3], IOaddr[4], cdm_8_mark5_1_p15[5], cdm_8_mark5_1_p15[6], cdm_8_mark5_1_p15[7], decoder_1_out1);  // AND_Gate
  // Probe on cdm_8_mark5_1_p11
  // Probe on cdm_8_mark5_1_p10
  // CdM_8_mark5 cdm_8_mark5_1: pin names not known; wires that end beside it: IRQ, vec, IAck, cdm_8_mark5_1_p4, cdm_8_mark5_1_p5, clk, cdm_8_mark5_1_p7, cdm_8_mark5_1_p8, cdm_8_mark5_1_p9, cdm_8_mark5_1_p10, cdm_8_mark5_1_p11, cdm_8_mark5_1_p12, cdm_8_mark5_1_p13, READwrite, {cdm_8_mark5_1_p15_2, cdm_8_mark5_1_p15, IOaddr}, cdm_8_mark5_1_p16, cdm_8_mark5_1_p17
  Decoder #(.disabled(0)) decoder_1 (
    .out0(decoder_1_out0), .out1(decoder_1_out1), .sel(cdm_8_mark5_1_p12), .en(cdm_8_mark5_1_p13));
  not not_1 (not_1_out, READwrite);
  assign IOdat = not_1_out ? cdm_8_mark5_1_p16 : 8'bz;  // Controlled_Buffer controlled_buffer_1
  assign cdm_8_mark5_1_p17 = READwrite ? IOdat : 8'bz;  // Controlled_Buffer controlled_buffer_2
  // Probe on {cdm_8_mark5_1_p15, IOaddr}
  not not_2 (not_2_out, clk);
  and and_3 (and_3_out, decoder_1_out1, ~IOsel);  // AND_Gate
  // Probe on IOdat
  RAM ram_1 (
    .addr({cdm_8_mark5_1_p15, IOaddr}), .data(IOdat), .sel(and_3_out), .clk(not_2_out), .ld(READwrite));  // open: clr
  ROM #(.addrWidth(16)) rom_1 (
    .addr({cdm_8_mark5_1_p15_2, cdm_8_mark5_1_p15, IOaddr}), .data(IOdat), .sel(decoder_1_out0));
  and I_O_0 (I_O_0_out, IOsel, ~IOaddr[0], ~IOaddr[1], ~IOaddr[2], ~IOaddr[3], ~IOaddr[4]);  // AND_Gate
  Decoder #(.disabled(0)) decoder_2 (.out0(decoder_2_out0), .out1(decoder_2_out1), .sel(READwrite), .en(I_O_0_out));
  OutputLogic outputlogic_1 (
    .I_O_addr(IOaddr), .I_O_sel(IOsel), .Read_write(READwrite), .I_O_dat(IOdat), .row(out_1),
    .o_number(5'b00001));
  assign IOdat = decoder_2_out1 ? \input  : 8'bz;  // Controlled_Buffer controlled_buffer_3
  assign {controlled_buffer_4_out, tick} = decoder_2_out0 ? IOdat : 8'bz;  // Controlled_Buffer controlled_buffer_4
  Pull_Resistor pull_resistor_1 (.node(tick));
  OutputLogic outputlogic_2 (
    .I_O_addr(IOaddr), .I_O_sel(IOsel), .Read_write(READwrite), .I_O_dat(IOdat), .row(out_2),
    .o_number(5'b00010));
  OutputLogic outputlogic_3 (
    .I_O_addr(IOaddr), .I_O_sel(IOsel), .Read_write(READwrite), .I_O_dat(IOdat), .row(out_3),
    .o_number(5'b00011));
  OutputLogic outputlogic_4 (
    .I_O_addr(IOaddr), .I_O_sel(IOsel), .Read_write(READwrite), .I_O_dat(IOdat), .row(out_4),
    .o_number(5'b00100));
  OutputLogic outputlogic_5 (
    .I_O_addr(IOaddr), .I_O_sel(IOsel), .Read_write(READwrite), .I_O_dat(IOdat), .row(out_5),
    .o_number(5'b00101));
  OutputLogic outputlogic_6 (
    .I_O_addr(IOaddr), .I_O_sel(IOsel), .Read_write(READwrite), .I_O_dat(IOdat), .row(out_6),
    .o_number(5'b00110));
  OutputLogic outputlogic_7 (
    .I_O_addr(IOaddr), .I_O_sel(IOsel), .Read_write(READwrite), .I_O_dat(IOdat), .row(out_7),
    .o_number(5'b00111));
  OutputLogic outputlogic_8 (
    .I_O_addr(IOaddr), .I_O_sel(IOsel), .Read_write(READwrite), .I_O_dat(IOdat), .row(out_8),
    .o_number(5'b01000));
  OutputLogic outputlogic_9 (
    .I_O_addr(IOaddr), .I_O_sel(IOsel), .Read_write(READwrite), .I_O_dat(IOdat), .row(out_9),
    .o_number(5'b01001));
  OutputLogic outputlogic_10 (
    .I_O_addr(IOaddr), .I_O_sel(IOsel), .Read_write(READwrite), .I_O_dat(IOdat), .row(out_10),
    .o_number(5'b01010));
  OutputLogic outputlogic_11 (
    .I_O_addr(IOaddr), .I_O_sel(IOsel), .Read_write(READwrite), .I_O_dat(IOdat), .row(out_11),
    .o_number(5'b01011));
  OutputLogic outputlogic_12 (
    .I_O_addr(IOaddr), .I_O_sel(IOsel), .Read_write(READwrite), .I_O_dat(IOdat), .row(out_12),
    .o_number(5'b01100));
  OutputLogic outputlogic_13 (
    .I_O_addr(IOaddr), .I_O_sel(IOsel), .Read_write(READwrite), .I_O_dat(IOdat), .row(out_13),
    .o_number(5'b01101));
  OutputLogic outputlogic_14 (
    .I_O_addr(IOaddr), .I_O_sel(IOsel), .Read_write(READwrite), .I_O_dat(IOdat), .row(out_14),
    .o_number(5'b01110));
  OutputLogic outputlogic_15 (
    .I_O_addr(IOaddr), .I_O_sel(IOsel), .Read_write(READwrite), .I_O_dat(IOdat), .row(out_15),
    .o_number(5'b01111));
  OutputLogic outputlogic_16 (
    .I_O_addr(IOaddr), .I_O_sel(IOsel), .Read_write(READwrite), .I_O_dat(IOdat), .row(out_16),
    .o_number(5'b10000));

  // Notes on the sheet:
  //   contents of rom_1 (hex, n*v repeats v):
  //   d6 66 0 d6 6f 1 d6 58 2 d6 7b 0 d6 50 0 d3 e0 bf f e0 3c d1 9 77 e1 1d d3 e0 bf d1 9 77 e0 13 d1 7
  //   77 e1 c d6 d5 0 d6 7b 0 d6 50 0 d3 9 ee e7 ee 19 d1 7 77 e1 c d6 d5 0 d6 7b 0 d6 50 0 ee 9 d0 e0 d1
  //   1 d2 0 a1 a2 ee c0 d6 6f 1 d6 58 2 d3 0 d0 e1 d2 10 a e4 7 a3 a3 8c 8a ee f8 d7 d0 e d1 1 d2 32 d3 0
  //   ac 12 a9 d2 1 12 a9 d3 e8 d2 d0 ab d7 d3 e0 bf f e0 3e d0 0 b1 d2 1 16 8b e1 4 d6 fb 1 8b e1 4 d6 a9
  //   1 8b e1 4 d6 1d 2 8b e1 4 d6 bf 1 8b e1 4 d6 61 1 8b e1 2 d7 8b e1 4 d6 d5 0 8b e1 4 d6 e5 0 8b 8b
  //   e1 4 d6 13 1 ee be d7 d0 32 d2 20 d3 0 a e4 6 a3 8c 8a ee f9 d0 1 d1 0 b5 14 a3 d7 d6 bf 0 d6 50 0
  //   d6 66 0 d6 6f 1 d6 58 2 d7 d6 bf 0 d6 50 0 d6 66 0 d3 e7 d0 c d1 32 11 d2 3 a6 ae 8d d2 0 ae 8d 8f
  //   d2 5 a6 ae 8d d2 0 ae 8f 8d d2 1 a6 ae 8a ae d6 58 2 d7 d6 bf 0 d6 50 0 d6 66 0 d3 e6 d0 a d1 32 11
  //   d2 3 a6 ae 8d d0 80 ac a4 8d 8f d2 2 a6 ae 8d ac a4 8d 8f d2 3 a6 ae 8d ac a4 4*8d 8f 8f d2 3 a6 ae
  //   8d ac a4 8d 8f d2 2 a6 ae 8d ac a4 8d 8f d2 3 a6 ae 8d a4 ac d6 58 2 d7 d0 1 d1 32 d2 0 ba 18 19 b0
  //   b6 62 a6 d7 d1 0 b5 d2 fe 49 d0 32 14 b0 d2 d0 ba a8 8d d0 32 14 b0 d2 d0 ba a8 d7 d1 0 b5 d2 fe 49
  //   d2 1 16 ba d0 32 14 b0 58 d2 d0 ba a8 8d d2 1 16 ba d0 32 14 b0 58 d2 d0 ba a8 d7 bb 93 e3 8 d3 80
  //   d6 d2 1 ee b d0 80 63 ab d6 87 1 d6 58 2 d7 bb 97 e3 8 d3 1 d6 d2 1 ee 8 ab d6 87 1 d6 58 2 d7 d1 0
  //   a9 d0 0 b0 d1 1 41 5 e1 8 8e 8c d1 0 a4 ee 6 8a 88 d1 0 a4 d2 1 12 f e5 4 ab ee 2 ab d6 87 1 d6 58 2
  //   d7 d6 6f 1 d3 1 d0 0 b1 77 ed d d0 d0 b1 89 a1 d3 fe d6 40 2 ee b d0 d0 d1 f0 a1 d3 1e d6 40 2 d7 d6
  //   6f 1 d3 1e d0 0 b1 77 eb e d0 d0 d1 e1 a1 d3 e2 d6 40 2 d7 ee b d0 d0 b1 8d a1 d3 2 d6 40 2 d7 d0 0
  //   b1 d2 1 16 b8 d1 0 a9 1e a8 d0 0 b2 1e a2 d6 87 1 d6 58 2 d7 d2 e0 d3 1 ab 8b ab d7
  //   read
endmodule

module OutputLogic (
  input  [4:0] I_O_addr,
  input  I_O_sel,
  input  Read_write,
  input  [7:0] I_O_dat,
  input  [4:0] o_number,
  output [15:0] row
);

  wire and_1_out, and_2_out, and_3_out, decoder_1_out0, I_O___number_out, not_1_out, not_2_out, not_3_out,
       not_4_out, not_5_out, not_6_out, not_7_out, not_8_out, not_9_out, not_10_out, register_3_q,
       xnor_1_out, xnor_2_out, xnor_3_out, xnor_4_out, xnor_5_out;
  wire [7:0] controlled_buffer_1_out;

  xnor xnor_1 (xnor_1_out, I_O_addr[0], o_number[0]);
  xnor xnor_2 (xnor_2_out, I_O_addr[1], o_number[1]);
  xnor xnor_3 (xnor_3_out, I_O_addr[2], o_number[2]);
  xnor xnor_4 (xnor_4_out, I_O_addr[3], o_number[3]);
  xnor xnor_5 (xnor_5_out, I_O_addr[4], o_number[4]);
  and I_O___number (I_O___number_out, I_O_sel, xnor_1_out, xnor_2_out, xnor_3_out, xnor_4_out, xnor_5_out);
  Decoder #(.disabled(0)) decoder_1 (.out0(decoder_1_out0), .sel(Read_write), .en(I_O___number_out));  // open: out1
  not not_1 (not_1_out, decoder_1_out0);
  not not_2 (not_2_out, not_1_out);
  not not_3 (not_3_out, not_2_out);
  not not_4 (not_4_out, not_3_out);
  assign controlled_buffer_1_out = decoder_1_out0 ? I_O_dat : 8'bz;  // Controlled_Buffer controlled_buffer_1
  Register register_1 (.D(controlled_buffer_1_out), .Q(row[15:8]), .clk(and_1_out));  // open: en, clr
  and and_1 (and_1_out, not_10_out, not_4_out);
  Register register_2 (.D(controlled_buffer_1_out), .Q(row[7:0]), .clk(and_2_out));  // open: en, clr
  not not_5 (not_5_out, decoder_1_out0);
  not not_6 (not_6_out, not_5_out);
  not not_7 (not_7_out, not_8_out);
  not not_8 (not_8_out, not_6_out);
  and and_2 (and_2_out, not_7_out, register_3_q);
  not not_9 (not_9_out, register_3_q);
  and and_3 (and_3_out, not_9_out, decoder_1_out0);
  not not_10 (not_10_out, register_3_q);
  Register #(.width(1), .trigger("falling")) register_3 (
    .D(and_3_out), .Q(register_3_q), .clk(decoder_1_out0));  // open: en, clr

  // Notes on the sheet:
  //   First write will change one row, the second write will change the other row
endmodule

module counter (
  input  nb1,
  input  nb2,
  input  nb3,
  input  nb4,
  input  nb5,
  input  nb6,
  input  nb7,
  input  nb8,
  input  nb1_2,
  input  nb2_2,
  input  nb3_2,
  input  nb4_2,
  input  nb5_2,
  input  nb6_2,
  input  nb7_2,
  input  nb8_2,
  output [7:0] total
);

  wire [1:0] adder_1_out, adder_2_out, adder_3_out, adder_4_out, adder_5_out, adder_6_out, adder_7_out,
       adder_8_out, adder_9_out, adder_10_out, adder_11_out, adder_12_out;
  wire [2:0] adder_13_out, adder_14_out;
  wire [2:2] adder_9_cout, adder_10_cout, adder_11_cout, adder_12_cout;

  Adder #(.width(1)) adder_1 (.a(nb1), .b(nb2), .out(adder_1_out[0]), .cout(adder_1_out[1]));  // open: cin
  Adder #(.width(1)) adder_2 (.a(nb3), .b(nb4), .out(adder_2_out[0]), .cout(adder_2_out[1]));  // open: cin
  Adder #(.width(1)) adder_3 (.a(nb5), .b(nb6), .out(adder_3_out[0]), .cout(adder_3_out[1]));  // open: cin
  Adder #(.width(1)) adder_4 (.a(nb7), .b(nb8), .out(adder_4_out[0]), .cout(adder_4_out[1]));  // open: cin
  Adder #(.width(1)) adder_5 (.a(nb1_2), .b(nb2_2), .out(adder_5_out[0]), .cout(adder_5_out[1]));  // open: cin
  Adder #(.width(1)) adder_6 (.a(nb3_2), .b(nb4_2), .out(adder_6_out[0]), .cout(adder_6_out[1]));  // open: cin
  Adder #(.width(1)) adder_7 (.a(nb5_2), .b(nb6_2), .out(adder_7_out[0]), .cout(adder_7_out[1]));  // open: cin
  Adder #(.width(1)) adder_8 (.a(nb7_2), .b(nb8_2), .out(adder_8_out[0]), .cout(adder_8_out[1]));  // open: cin
  Adder #(.width(2)) adder_9 (
    .a(adder_1_out), .b(adder_2_out), .out(adder_9_out), .cout(adder_9_cout[2]));  // open: cin
  Adder #(.width(2)) adder_10 (
    .a(adder_3_out), .b(adder_4_out), .out(adder_10_out), .cout(adder_10_cout[2]));  // open: cin
  Adder #(.width(2)) adder_11 (
    .a(adder_5_out), .b(adder_6_out), .out(adder_11_out), .cout(adder_11_cout[2]));  // open: cin
  Adder #(.width(2)) adder_12 (
    .a(adder_7_out), .b(adder_8_out), .out(adder_12_out), .cout(adder_12_cout[2]));  // open: cin
  Adder #(.width(3)) adder_13 (
    .a({adder_9_cout[2], adder_9_out}), .b({adder_10_cout[2], adder_10_out}), .out(adder_13_out));  // open: cin, cout
  Adder #(.width(3)) adder_14 (
    .a({adder_11_cout[2], adder_11_out}), .b({adder_12_cout[2], adder_12_out}), .out(adder_14_out));  // open: cin, cout
  Adder #(.width(3)) adder_15 (.a(adder_13_out), .b(adder_14_out), .out(total[2:0]), .cout(total[3]));  // open: cin

  assign total[7:4] = 4'b0000;

  // Notes on the sheet:
  //   Соседи
  //   Соседи
endmodule

module PressedCounter (
  input  [15:0] Pressed_1,
  input  [15:0] Pressed_2,
  input  [15:0] Pressed_3,
  input  [15:0] Pressed_4,
  input  [15:0] Pressed_5,
  input  [15:0] Pressed_6,
  input  [15:0] Pressed_7,
  input  [15:0] Pressed_8,
  input  [15:0] Pressed_9,
  input  [15:0] Pressed_10,
  input  [15:0] Pressed_11,
  input  [15:0] Pressed_12,
  input  [15:0] Pressed_13,
  input  [15:0] Pressed_14,
  input  [15:0] Pressed_15,
  input  [15:0] Pressed_16,
  output [8:0] ouot
);

  wire [7:0] adder_1_out, adder_2_out, adder_3_out, adder_4_out, adder_5_out, adder_6_out, adder_7_out,
       adder_8_out, adder_9_out, adder_10_out, adder_11_out, adder_12_out, adder_13_out, adder_14_out,
       counter_1_total, counter_2_total, counter_3_total, counter_4_total, counter_5_total, counter_6_total,
       counter_7_total, counter_8_total, counter_9_total, counter_10_total, counter_11_total,
       counter_12_total, counter_13_total, counter_14_total, counter_15_total, counter_16_total;

  counter counter_1 (
    .nb1(Pressed_1[0]), .nb2(Pressed_1[1]), .nb3(Pressed_1[2]), .nb4(Pressed_1[3]), .nb5(Pressed_1[4]),
    .nb6(Pressed_1[5]), .nb7(Pressed_1[6]), .nb8(Pressed_1[7]), .nb1_2(Pressed_1[8]), .nb2_2(Pressed_1[9]),
    .nb3_2(Pressed_1[10]), .nb4_2(Pressed_1[11]), .nb5_2(Pressed_1[12]), .nb6_2(Pressed_1[13]),
    .nb7_2(Pressed_1[14]), .nb8_2(Pressed_1[15]), .total(counter_1_total));
  counter counter_2 (
    .nb1(Pressed_2[0]), .nb2(Pressed_2[1]), .nb3(Pressed_2[2]), .nb4(Pressed_2[3]), .nb5(Pressed_2[4]),
    .nb6(Pressed_2[5]), .nb7(Pressed_2[6]), .nb8(Pressed_2[7]), .nb1_2(Pressed_2[8]), .nb2_2(Pressed_2[9]),
    .nb3_2(Pressed_2[10]), .nb4_2(Pressed_2[11]), .nb5_2(Pressed_2[12]), .nb6_2(Pressed_2[13]),
    .nb7_2(Pressed_2[14]), .nb8_2(Pressed_2[15]), .total(counter_2_total));
  counter counter_3 (
    .nb1(Pressed_3[0]), .nb2(Pressed_3[1]), .nb3(Pressed_3[2]), .nb4(Pressed_3[3]), .nb5(Pressed_3[4]),
    .nb6(Pressed_3[5]), .nb7(Pressed_3[6]), .nb8(Pressed_3[7]), .nb1_2(Pressed_3[8]), .nb2_2(Pressed_3[9]),
    .nb3_2(Pressed_3[10]), .nb4_2(Pressed_3[11]), .nb5_2(Pressed_3[12]), .nb6_2(Pressed_3[13]),
    .nb7_2(Pressed_3[14]), .nb8_2(Pressed_3[15]), .total(counter_3_total));
  counter counter_4 (
    .nb1(Pressed_4[0]), .nb2(Pressed_4[1]), .nb3(Pressed_4[2]), .nb4(Pressed_4[3]), .nb5(Pressed_4[4]),
    .nb6(Pressed_4[5]), .nb7(Pressed_4[6]), .nb8(Pressed_4[7]), .nb1_2(Pressed_4[8]), .nb2_2(Pressed_4[9]),
    .nb3_2(Pressed_4[10]), .nb4_2(Pressed_4[11]), .nb5_2(Pressed_4[12]), .nb6_2(Pressed_4[13]),
    .nb7_2(Pressed_4[14]), .nb8_2(Pressed_4[15]), .total(counter_4_total));
  counter counter_5 (
    .nb1(Pressed_5[0]), .nb2(Pressed_5[1]), .nb3(Pressed_5[2]), .nb4(Pressed_5[3]), .nb5(Pressed_5[4]),
    .nb6(Pressed_5[5]), .nb7(Pressed_5[6]), .nb8(Pressed_5[7]), .nb1_2(Pressed_5[8]), .nb2_2(Pressed_5[9]),
    .nb3_2(Pressed_5[10]), .nb4_2(Pressed_5[11]), .nb5_2(Pressed_5[12]), .nb6_2(Pressed_5[13]),
    .nb7_2(Pressed_5[14]), .nb8_2(Pressed_5[15]), .total(counter_5_total));
  counter counter_6 (
    .nb1(Pressed_6[0]), .nb2(Pressed_6[1]), .nb3(Pressed_6[2]), .nb4(Pressed_6[3]), .nb5(Pressed_6[4]),
    .nb6(Pressed_6[5]), .nb7(Pressed_6[6]), .nb8(Pressed_6[7]), .nb1_2(Pressed_6[8]), .nb2_2(Pressed_6[9]),
    .nb3_2(Pressed_6[10]), .nb4_2(Pressed_6[11]), .nb5_2(Pressed_6[12]), .nb6_2(Pressed_6[13]),
    .nb7_2(Pressed_6[14]), .nb8_2(Pressed_6[15]), .total(counter_6_total));
  counter counter_7 (
    .nb1(Pressed_7[0]), .nb2(Pressed_7[1]), .nb3(Pressed_7[2]), .nb4(Pressed_7[3]), .nb5(Pressed_7[4]),
    .nb6(Pressed_7[5]), .nb7(Pressed_7[6]), .nb8(Pressed_7[7]), .nb1_2(Pressed_7[8]), .nb2_2(Pressed_7[9]),
    .nb3_2(Pressed_7[10]), .nb4_2(Pressed_7[11]), .nb5_2(Pressed_7[12]), .nb6_2(Pressed_7[13]),
    .nb7_2(Pressed_7[14]), .nb8_2(Pressed_7[15]), .total(counter_7_total));
  counter counter_8 (
    .nb1(Pressed_8[0]), .nb2(Pressed_8[1]), .nb3(Pressed_8[2]), .nb4(Pressed_8[3]), .nb5(Pressed_8[4]),
    .nb6(Pressed_8[5]), .nb7(Pressed_8[6]), .nb8(Pressed_8[7]), .nb1_2(Pressed_8[8]), .nb2_2(Pressed_8[9]),
    .nb3_2(Pressed_8[10]), .nb4_2(Pressed_8[11]), .nb5_2(Pressed_8[12]), .nb6_2(Pressed_8[13]),
    .nb7_2(Pressed_8[14]), .nb8_2(Pressed_8[15]), .total(counter_8_total));
  counter counter_9 (
    .nb1(Pressed_9[0]), .nb2(Pressed_9[1]), .nb3(Pressed_9[2]), .nb4(Pressed_9[3]), .nb5(Pressed_9[4]),
    .nb6(Pressed_9[5]), .nb7(Pressed_9[6]), .nb8(Pressed_9[7]), .nb1_2(Pressed_9[8]), .nb2_2(Pressed_9[9]),
    .nb3_2(Pressed_9[10]), .nb4_2(Pressed_9[11]), .nb5_2(Pressed_9[12]), .nb6_2(Pressed_9[13]),
    .nb7_2(Pressed_9[14]), .nb8_2(Pressed_9[15]), .total(counter_9_total));
  counter counter_10 (
    .nb1(Pressed_10[0]), .nb2(Pressed_10[1]), .nb3(Pressed_10[2]), .nb4(Pressed_10[3]), .nb5(Pressed_10[4]),
    .nb6(Pressed_10[5]), .nb7(Pressed_10[6]), .nb8(Pressed_10[7]), .nb1_2(Pressed_10[8]),
    .nb2_2(Pressed_10[9]), .nb3_2(Pressed_10[10]), .nb4_2(Pressed_10[11]), .nb5_2(Pressed_10[12]),
    .nb6_2(Pressed_10[13]), .nb7_2(Pressed_10[14]), .nb8_2(Pressed_10[15]), .total(counter_10_total));
  counter counter_11 (
    .nb1(Pressed_11[0]), .nb2(Pressed_11[1]), .nb3(Pressed_11[2]), .nb4(Pressed_11[3]), .nb5(Pressed_11[4]),
    .nb6(Pressed_11[5]), .nb7(Pressed_11[6]), .nb8(Pressed_11[7]), .nb1_2(Pressed_11[8]),
    .nb2_2(Pressed_11[9]), .nb3_2(Pressed_11[10]), .nb4_2(Pressed_11[11]), .nb5_2(Pressed_11[12]),
    .nb6_2(Pressed_11[13]), .nb7_2(Pressed_11[14]), .nb8_2(Pressed_11[15]), .total(counter_11_total));
  counter counter_12 (
    .nb1(Pressed_12[0]), .nb2(Pressed_12[1]), .nb3(Pressed_12[2]), .nb4(Pressed_12[3]), .nb5(Pressed_12[4]),
    .nb6(Pressed_12[5]), .nb7(Pressed_12[6]), .nb8(Pressed_12[7]), .nb1_2(Pressed_12[8]),
    .nb2_2(Pressed_12[9]), .nb3_2(Pressed_12[10]), .nb4_2(Pressed_12[11]), .nb5_2(Pressed_12[12]),
    .nb6_2(Pressed_12[13]), .nb7_2(Pressed_12[14]), .nb8_2(Pressed_12[15]), .total(counter_12_total));
  counter counter_13 (
    .nb1(Pressed_13[0]), .nb2(Pressed_13[1]), .nb3(Pressed_13[2]), .nb4(Pressed_13[3]), .nb5(Pressed_13[4]),
    .nb6(Pressed_13[5]), .nb7(Pressed_13[6]), .nb8(Pressed_13[7]), .nb1_2(Pressed_13[8]),
    .nb2_2(Pressed_13[9]), .nb3_2(Pressed_13[10]), .nb4_2(Pressed_13[11]), .nb5_2(Pressed_13[12]),
    .nb6_2(Pressed_13[13]), .nb7_2(Pressed_13[14]), .nb8_2(Pressed_13[15]), .total(counter_13_total));
  counter counter_14 (
    .nb1(Pressed_14[0]), .nb2(Pressed_14[1]), .nb3(Pressed_14[2]), .nb4(Pressed_14[3]), .nb5(Pressed_14[4]),
    .nb6(Pressed_14[5]), .nb7(Pressed_14[6]), .nb8(Pressed_14[7]), .nb1_2(Pressed_14[8]),
    .nb2_2(Pressed_14[9]), .nb3_2(Pressed_14[10]), .nb4_2(Pressed_14[11]), .nb5_2(Pressed_14[12]),
    .nb6_2(Pressed_14[13]), .nb7_2(Pressed_14[14]), .nb8_2(Pressed_14[15]), .total(counter_14_total));
  counter counter_15 (
    .nb1(Pressed_15[0]), .nb2(Pressed_15[1]), .nb3(Pressed_15[2]), .nb4(Pressed_15[3]), .nb5(Pressed_15[4]),
    .nb6(Pressed_15[5]), .nb7(Pressed_15[6]), .nb8(Pressed_15[7]), .nb1_2(Pressed_15[8]),
    .nb2_2(Pressed_15[9]), .nb3_2(Pressed_15[10]), .nb4_2(Pressed_15[11]), .nb5_2(Pressed_15[12]),
    .nb6_2(Pressed_15[13]), .nb7_2(Pressed_15[14]), .nb8_2(Pressed_15[15]), .total(counter_15_total));
  counter counter_16 (
    .nb1(Pressed_16[0]), .nb2(Pressed_16[1]), .nb3(Pressed_16[2]), .nb4(Pressed_16[3]), .nb5(Pressed_16[4]),
    .nb6(Pressed_16[5]), .nb7(Pressed_16[6]), .nb8(Pressed_16[7]), .nb1_2(Pressed_16[8]),
    .nb2_2(Pressed_16[9]), .nb3_2(Pressed_16[10]), .nb4_2(Pressed_16[11]), .nb5_2(Pressed_16[12]),
    .nb6_2(Pressed_16[13]), .nb7_2(Pressed_16[14]), .nb8_2(Pressed_16[15]), .total(counter_16_total));
  Adder adder_1 (.a(counter_1_total), .b(counter_2_total), .out(adder_1_out));  // open: cin, cout
  Adder adder_2 (.a(counter_3_total), .b(counter_4_total), .out(adder_2_out));  // open: cin, cout
  Adder adder_3 (.a(counter_5_total), .b(counter_6_total), .out(adder_3_out));  // open: cin, cout
  Adder adder_4 (.a(counter_7_total), .b(counter_8_total), .out(adder_4_out));  // open: cin, cout
  Adder adder_5 (.a(counter_9_total), .b(counter_10_total), .out(adder_5_out));  // open: cin, cout
  Adder adder_6 (.a(counter_11_total), .b(counter_12_total), .out(adder_6_out));  // open: cin, cout
  Adder adder_7 (.a(counter_13_total), .b(counter_14_total), .out(adder_7_out));  // open: cin, cout
  Adder adder_8 (.a(counter_15_total), .b(counter_16_total), .out(adder_8_out));  // open: cin, cout
  Adder adder_9 (.a(adder_1_out), .b(adder_2_out), .out(adder_9_out));  // open: cin, cout
  Adder adder_10 (.a(adder_3_out), .b(adder_4_out), .out(adder_10_out));  // open: cin, cout
  Adder adder_11 (.a(adder_5_out), .b(adder_6_out), .out(adder_11_out));  // open: cin, cout
  Adder adder_12 (.a(adder_7_out), .b(adder_8_out), .out(adder_12_out));  // open: cin, cout
  Adder adder_13 (.a(adder_9_out), .b(adder_10_out), .out(adder_13_out));  // open: cin, cout
  Adder adder_14 (.a(adder_11_out), .b(adder_12_out), .out(adder_14_out));  // open: cin, cout
  Adder adder_15 (.a(adder_13_out), .b(adder_14_out), .out(ouot[7:0]), .cout(ouot[8]));  // open: cin
  // Probe on ouot
endmodule

module BUTTONS (
  input  u,
  input  ok,
  input  l,
  input  r,
  input  d,
  input  start,
  input  reset,
  input  glider,
  input  pause,
  input  pause_2,
  output [15:0] out_11,
  output [15:0] out_12,
  output [15:0] out_13,
  output [15:0] out_14,
  output [15:0] out_15,
  output [15:0] out_16,
  output [15:0] out_17,
  output [15:0] out_18,
  output [15:0] out_19,
  output [15:0] out_20,
  output [15:0] out_21,
  output [15:0] out_22,
  output [15:0] out_23,
  output [15:0] out_24,
  output [15:0] out_25,
  output [15:0] out_26,
  output [8:0] out_27
);

  wire controller_1_tick, transistor_1_out;
  wire [7:0] controlled_buffer_1_out;
  wire [15:0] controller_1_out_1, controller_1_out_2, controller_1_out_3, controller_1_out_4,
       controller_1_out_5, controller_1_out_6, controller_1_out_7, controller_1_out_8, controller_1_out_9,
       controller_1_out_10, controller_1_out_11, controller_1_out_12, controller_1_out_13,
       controller_1_out_14, controller_1_out_15, controller_1_out_16;

  assign controlled_buffer_1_out = ok ? 8'h5 : 8'bz;  // Controlled_Buffer controlled_buffer_1
  Transistor #(.\type ("n")) transistor_1 (.in(1'b0), .out(transistor_1_out), .gate(ok));
  assign controlled_buffer_1_out = l ? 8'h4 : 8'bz;  // Controlled_Buffer controlled_buffer_2
  assign controlled_buffer_1_out = reset ? 8'h7 : 8'bz;  // Controlled_Buffer controlled_buffer_3
  Transistor #(.\type ("n")) transistor_2 (.in(1'b0), .out(transistor_1_out), .gate(l));
  Transistor #(.\type ("n")) transistor_3 (.in(1'b0), .out(transistor_1_out), .gate(d));
  assign controlled_buffer_1_out = d ? 8'h3 : 8'bz;  // Controlled_Buffer controlled_buffer_4
  assign controlled_buffer_1_out = glider ? 8'h8 : 8'bz;  // Controlled_Buffer controlled_buffer_5
  Transistor #(.\type ("n")) transistor_4 (.in(1'b0), .out(transistor_1_out), .gate(u));
  Transistor #(.\type ("n")) transistor_5 (.in(1'b0), .out(transistor_1_out), .gate(r));
  assign controlled_buffer_1_out = r ? 8'h2 : 8'bz;  // Controlled_Buffer controlled_buffer_6
  assign controlled_buffer_1_out = u ? 8'h1 : 8'bz;  // Controlled_Buffer controlled_buffer_7
  assign controlled_buffer_1_out = pause ? 8'h9 : 8'bz;  // Controlled_Buffer controlled_buffer_8
  Pull_Resistor #(.pull(1)) pull_resistor_1 (.node(transistor_1_out));
  assign controlled_buffer_1_out = start ? 8'h6 : 8'bz;  // Controlled_Buffer controlled_buffer_9
  Rows_plate rows_plate_1 (
    .tick(controller_1_tick), .Pressed_1(controller_1_out_1), .Pressed_2(controller_1_out_2),
    .Pressed_3(controller_1_out_3), .Pressed_4(controller_1_out_4), .Pressed_5(controller_1_out_5),
    .Pressed_6(controller_1_out_6), .Pressed_7(controller_1_out_7), .Pressed_8(controller_1_out_8),
    .Pressed_9(controller_1_out_9), .Pressed_10(controller_1_out_10), .Pressed_11(controller_1_out_11),
    .Pressed_12(controller_1_out_12), .Pressed_13(controller_1_out_13), .Pressed_14(controller_1_out_14),
    .Pressed_15(controller_1_out_15), .Pressed_16(controller_1_out_16), .out_1(out_11), .out_2(out_19),
    .out_3(out_12), .out_4(out_20), .out_5(out_13), .out_6(out_21), .out_7(out_14), .out_8(out_22),
    .out_9(out_15), .out_10(out_23), .out_11(out_16), .out_12(out_24), .out_13(out_17), .out_14(out_25),
    .out_15(out_18), .out_16(out_26), .alive(out_27));
  Controller controller_1 (
    .tick(controller_1_tick), .out_1(controller_1_out_1), .out_2(controller_1_out_2),
    .out_3(controller_1_out_3), .out_4(controller_1_out_4), .out_5(controller_1_out_5),
    .out_6(controller_1_out_6), .out_7(controller_1_out_7), .out_8(controller_1_out_8),
    .out_9(controller_1_out_9), .out_10(controller_1_out_10), .out_11(controller_1_out_11),
    .out_12(controller_1_out_12), .out_13(controller_1_out_13), .out_14(controller_1_out_14),
    .out_15(controller_1_out_15), .out_16(controller_1_out_16), .\input (controlled_buffer_1_out));
  assign controlled_buffer_1_out = pause_2 ? 8'ha : 8'bz;  // Controlled_Buffer controlled_buffer_10
endmodule
